# Fritzing sketch Babycakes (saved by Fritzing 1.0.2b)

parts:
  BLDC1 = CTRE Falcon 500 [part_number=19-708850]
  BLDC2 = CTRE Falcon 500 [part_number=19-708850]
  BLDC3 = CTRE Falcon 500 [part_number=19-708850]
  BLDC4 = CTRE Falcon 500 [part_number=19-708850]
  BLDC5 = REV NEO 550 BLDC Motor [part_number=REV-21-1651]
  BLDC6 = REV NEO 550 BLDC Motor [part_number=REV-21-1651]
  BLDC7 = REV NEO 550 BLDC Motor [part_number=REV-21-1651]
  BLDC8 = REV NEO 550 BLDC Motor [part_number=REV-21-1651]
  PDH1 = rev_pdh
  ctrl1 = rev_spark_max [part_number=rev-11-2158]
  ctrl1_2 = rev_spark_max [part_number=rev-11-2158]
  ctrl1_3 = rev_spark_max [part_number=rev-11-2158]
  ctrl1_4 = rev_spark_max [part_number=rev-11-2158]
  Mini_Power_Module1 = REV Mini Power Module [form="♀ (female)" package=THT]
  LED1 = LED - 5mm [color="Red (633nm)" current=0.030A package="5 mm [THT]"]
  ctrl1_5 = rev_spark_max [part_number=rev-11-2158]
  BLDC9 = REV NEO BLDC Motor [part_number=REV-21-1650]
  ctrl1_6 = rev_spark_max [part_number=rev-11-2158]
  BLDC10 = REV NEO BLDC Motor [part_number=REV-21-1650]
  ctrl1_7 = rev_spark_max [part_number=rev-11-2158]
  BLDC12 = REV NEO BLDC Motor [part_number=REV-21-1650]
  ctrl1_8 = rev_spark_max [part_number=rev-11-2158]
  ctrl1_9 = rev_spark_max [part_number=rev-11-2158]
  BLDC13 = REV NEO BLDC Motor [part_number=REV-21-1650]
  BLDC14 = REV NEO BLDC Motor [part_number=REV-21-1650]
  ctrl1_10 = rev_spark_max [part_number=rev-11-2158]
  ctrl1_11 = rev_spark_max [part_number=rev-11-2158]
  BLDC15 = REV NEO BLDC Motor [part_number=REV-21-1650]
  BLDC16 = REV NEO BLDC Motor [part_number=REV-21-1650]
  ctrl1_12 = rev_spark_max [part_number=rev-11-2158]
  ctrl1_13 = rev_spark_max [part_number=rev-11-2158]
  BLDC17 = REV NEO BLDC Motor [part_number=REV-21-1650]
  BLDC18 = REV NEO BLDC Motor [part_number=REV-21-1650]
  ctrl1_14 = rev_spark_max [part_number=rev-11-2158]
  BLDC19 = REV NEO BLDC Motor [part_number=REV-21-1650]
  NetSw1 = Brainboxes Ethernet Switch [part_number=SW-005 package="DIN 101x101mm"]  # not connected
  CAM1 = Limelight 2plus  # not connected
  BAT1 = Battery 12V [package=battcom_20mm_pth]
  Pigeon_2_1 = CTRE Pigeon 2.0 [package=THT]  # not connected
  CB1 = Thermal Circuit Breaker [package=waterproof]
  M1 = IR break beam 3mm rx [package=THT]  # not connected
  M2 = IR break beam 3mm rx [package=THT]  # not connected
  Raspberry_Pi_1 = Raspberry Pi 3 [part_number=RPI-3-V1.2]  # not connected

nets:
  N1: BLDC1.Vin-, PDH1.connector19
  N2: BLDC1.Vin+, PDH1.connector18
  N3: BLDC2.Vin-, PDH1.connector15
  N4: BLDC2.Vin+, PDH1.connector14
  N5: BLDC3.Vin-, PDH1.connector7
  N6: BLDC3.Vin+, PDH1.connector6
  N7: BLDC4.Vin-, PDH1.connector11
  N8: BLDC4.Vin+, PDH1.connector10
  N9: BLDC5.A, ctrl1.connector18
  N10: BLDC5.B, ctrl1.connector2
  N11: BLDC5.C, ctrl1.connector3
  N12: BLDC6.A, ctrl1_2.connector18
  N13: BLDC6.B, ctrl1_2.connector2
  N14: BLDC6.C, ctrl1_2.connector3
  N15: BLDC7.A, ctrl1_3.connector18
  N16: BLDC7.B, ctrl1_3.connector2
  N17: BLDC7.C, ctrl1_3.connector3
  N18: BLDC8.A, ctrl1_4.connector18
  N19: BLDC8.B, ctrl1_4.connector2
  N20: BLDC8.C, ctrl1_4.connector3
  N21: PDH1.connector0, LED1.cathode
  N22: PDH1.connector1, LED1.anode
  N23: PDH1.connector2, Mini_Power_Module1.Input_+
  N24: PDH1.connector3, Mini_Power_Module1.Input_-
  N25: PDH1.connector4, ctrl1_4.connector0
  N26: PDH1.connector5, ctrl1_4.connector1
  N27: PDH1.connector8, ctrl1_3.connector0
  N28: PDH1.connector9, ctrl1_3.connector1
  N29: PDH1.connector12, ctrl1_2.connector0
  N30: PDH1.connector13, ctrl1_2.connector1
  N31: PDH1.connector16, ctrl1.connector0
  N32: PDH1.connector17, ctrl1.connector1
  N33: PDH1.connector20, ctrl1_5.connector0
  N34: PDH1.connector21, ctrl1_5.connector1
  N35: PDH1.connector22, ctrl1_6.connector0
  N36: PDH1.connector23, ctrl1_6.connector1
  N37: PDH1.connector24, ctrl1_7.connector0
  N38: PDH1.connector25, ctrl1_7.connector1
  N39: PDH1.connector26, ctrl1_8.connector1
  N40: PDH1.connector27, ctrl1_8.connector0
  N41: PDH1.connector28, ctrl1_9.connector1
  N42: PDH1.connector29, ctrl1_9.connector0
  N43: PDH1.connector30, ctrl1_14.connector1
  N44: PDH1.connector31, ctrl1_14.connector0
  N45: PDH1.connector32, ctrl1_11.connector1
  N46: PDH1.connector33, ctrl1_11.connector0
  N47: PDH1.connector34, ctrl1_10.connector1
  N48: PDH1.connector35, ctrl1_10.connector0
  N49: PDH1.connector36, ctrl1_12.connector1
  N50: PDH1.connector37, ctrl1_12.connector0
  N51: PDH1.connector38, ctrl1_13.connector1
  N52: PDH1.connector39, ctrl1_13.connector0
  N53: PDH1.connector44, BAT1.-
  N54: PDH1.connector45, CB1.1
  N55: ctrl1_5.connector2, BLDC9.B
  N56: ctrl1_5.connector3, BLDC9.A
  N57: ctrl1_5.connector18, BLDC9.C
  N58: ctrl1_6.connector2, BLDC10.B
  N59: ctrl1_6.connector3, BLDC10.A
  N60: ctrl1_6.connector18, BLDC10.C
  N61: ctrl1_7.connector2, BLDC12.B
  N62: ctrl1_7.connector3, BLDC12.A
  N63: ctrl1_7.connector18, BLDC12.C
  N64: ctrl1_8.connector2, BLDC13.B
  N65: ctrl1_8.connector3, BLDC13.A
  N66: ctrl1_8.connector18, BLDC13.C
  N67: ctrl1_9.connector2, BLDC14.B
  N68: ctrl1_9.connector3, BLDC14.A
  N69: ctrl1_9.connector18, BLDC14.C
  N70: ctrl1_10.connector2, BLDC16.B
  N71: ctrl1_10.connector3, BLDC16.A
  N72: ctrl1_10.connector18, BLDC16.C
  N73: ctrl1_11.connector2, BLDC15.B
  N74: ctrl1_11.connector3, BLDC15.A
  N75: ctrl1_11.connector18, BLDC15.C
  N76: ctrl1_12.connector2, BLDC17.B
  N77: ctrl1_12.connector3, BLDC17.A
  N78: ctrl1_12.connector18, BLDC17.C
  N79: ctrl1_13.connector2, BLDC18.B
  N80: ctrl1_13.connector3, BLDC18.A
  N81: ctrl1_13.connector18, BLDC18.C
  N82: ctrl1_14.connector2, BLDC19.B
  N83: ctrl1_14.connector18, BLDC19.C
  N84: BAT1.+, CB1.2

notes:
  Blinkin Stand-in
  Intake
  Feeder
  Shooter
  Climber
  Pivot
  Shooter Slider (Trap)

custom parts:
  CTRE Falcon 500: The Falcon 500 powered by Talon FX is a brushless motor with an integrated motor controller and high-resolution encoder, custom designed specifically for the FIRST Robotics Competition, through a collaboration between Cross the Road Electronics and VEX Robotics.
  REV NEO 550 BLDC Motor: The REV NEO 550 Brushless Motor is the newest member in the NEO family of brushless motors. Its output power and small size are specifically designed to make NEO 550 the perfect motor for intakes and other non-drivetrain robot mechanisms. Mounting holes and pilot match a standard 550 series motor, making it natively mount to many existing off-the-shelf gearboxes.
  REV Mini Power Module: Generic female header
  REV NEO BLDC Motor: The REV NEO Brushless Motor is the first brushless motor designed to meet the unique demands of the FRC community. NEO offers an incredible power density due to its compact size and reduced weight. As it is designed to have similar performance characteristics and matching mounting features, NEO can be a drop-in replacement for CIM-style motors.
  Brainboxes Ethernet Switch: Light Industrial/Commercial Ethernet 5 Port unmanaged switch. Galvanically Isolated Ports. Power supply with wide voltage range means it can be powered from USB or on the 24V factory floor. Power terminal is removable with for easy wiring. Power consumption is optimised based on the status of the link device. No software required. Ideal for factory floor, in vehicle and marine applications.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
  Limelight 2plus: Limelight makes reliable FRC vision accessible to all teams, regardless of programming ability and time constraints. Vision has never been easier. Limelight 2+ takes the Einstein-proven Limelight 2 and perfects it. Its internals have been redesigned to: - Reduce power consumption by up to 50% - Eliminate the LED "warm-up" period. - Further improve low voltage performance, dropping the brownout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
  Battery 12V: Battery Holders Various common sizes : AA, AAA, 20mm coin cell and 12mm coin cell.
  CTRE Pigeon 2.0: Generic single row SMD female header
  Thermal Circuit Breaker: Cooper Bussman P/N CB185-120, CB185F-120, CB285-120 CB285F-120, CB285120F or Optifuse P/N 153120, 253120
  IR break beam 3mm rx: Infrared break beam Sensor rx module.
