# Fritzing sketch Electrical Diagram (saved by Fritzing 1.0.2b)
breadboards: 1

parts:
  CAM1 = Limelight 2plus
  NetSw1 = Brainboxes Ethernet Switch [part_number=SW-005 package="DIN 101x101mm"]
  cntl1 = roborio_v2
  TBE1 = REV Through Bore Encoder
  RSL1 = FRC Robot Signal Light [part_number=855PB-B12ME522]

nets (from the breadboard view):
  N1: CAM1.ETH0, NetSw1.eth1
  N2: cntl1.connector24, TBE1.V
  N3: cntl1.connector25, TBE1.B
  N4: cntl1.connector26, TBE1.Z
  N5: cntl1.connector41, RSL1.anode1
  N6: cntl1.connector42, RSL1.anode0

custom parts:
  Limelight 2plus: Limelight makes reliable FRC vision accessible to all teams, regardless of programming ability and time constraints. Vision has never been easier. Limelight 2+ takes the Einstein-proven Limelight 2 and perfects it. Its internals have been redesigned to: - Reduce power consumption by up to 50% - Eliminate the LED "warm-up" period. - Further improve low voltage performance, dropping the brownout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
  Brainboxes Ethernet Switch: Light Industrial/Commercial Ethernet 5 Port unmanaged switch. Galvanically Isolated Ports. Power supply with wide voltage range means it can be powered from USB or on the 24V factory floor. Power terminal is removable with for easy wiring. Power consumption is optimised based on the status of the link device. No software required. Ideal for factory floor, in vehicle and marine applications.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
  REV Through Bore Encoder: The REV Through Bore Encoder is specifically designed with the end user in mind, allowing teams to place sensors in the locations closest to the rotation that they wish to measure. This rotary sensor measures both relative and absolute position through its ABI quadrature output and its absolute position pulse output. Mounting an encoder has never been easier with a 1/2in Hex Through Bore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
  FRC Robot Signal Light: Panel Mount Beacon,12V AC/DC,45 mm Panel Mounting LED,Amber,22.5 mm Round Mounting Hole Used as: R709 *ROBOTS must have a signal light. ROBOTS must use at least 1, but no more than 2, diagnostic ROBOT Signal Light (RSL) (P/N 855PB-B12ME522). Any RSL must be: A. mounted on the ROBOT such that it is easily visible while standing 3 ft. (~ 100 cm) in front of the ROBOT, B. connected to the “RSL”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
